# Fritzing sketch two_motors (saved by Fritzing 0.9.3b)
breadboards: 1

parts:
  Part3 = Arduino Uno (Rev3) - ICSP
  Part4 = EasyDriver_v44
  M2 = Stepper Motor - Bipolar
  S2 = Pushbutton [package="[THT]"]

nets:
  N1: Part3.D8, Part4.DIR
  N2: Part3.D9_PWM, Part4.STEP
  N3: Part3.D4, S2.Pin_1, S2.Pin_2
  N4: Part4.GND, S2.Pin_3, S2.Pin_4
  N5: Part4.OUT2A, M2.A
  N6: Part4.OUT2B, M2.C
  N7: Part4.OUT1A, M2.B
  N8: Part4.OUT1B, M2.D
